// Logisim project ALU.circ as structural Verilog: 2 circuits, main circuit ALU
module ALU (
  input  [4:0] Shift,
  input  [31:0] A,
  input  [31:0] B,
  input  CarryIn,
  input  [3:0] Codop,
  output [31:0] S,
  output [3:0] Flags
);

  wire bitselector_4_out, bitselector_5_out, bitselector_6_out, C3, C6, C7, C8, C10, C11, C12, C45,
       not_1_out, s1, xnor_1_out, xor_1_out;
  wire [4:0] negator_1_out, subtractor_5_out;
  wire [31:0] AAND, ADC, ASR, BIC, CMN, CMP, EOR, LSL, LSR, MUL, MVN, not_2_out, ORR, RROR, RSB, S_t, SBC,
       subtractor_1_out, TST;

  assign AAND = A & B;  // AND_Gate AAND, 32 bits wide
  assign EOR = A ^ B;  // XOR_Gate EOR, 32 bits wide
  Shifter #(.width(32)) shifter_1 (.in(B), .\dist (Shift), .out(LSL));
  Shifter #(.width(32), .shift("lr")) shifter_2 (.in(B), .\dist (Shift), .out(LSR));
  Shifter #(.width(32), .shift("ar")) shifter_3 (.in(B), .\dist (Shift), .out(ASR));
  Adder #(.width(32)) adder_1 (.a(A), .b(B), .out(ADC), .cin(CarryIn), .cout(C6));
  not not_1 (not_1_out, CarryIn);
  Subtractor #(.width(32)) subtractor_1 (.a(A), .b(B), .out(subtractor_1_out), .bin(not_1_out), .bout(s1));
  Shifter #(.width(32), .shift("rl")) shifter_4 (.in(B), .\dist (Shift), .out(RROR));
  Subtractor #(.width(32)) subtractor_2 (.a(subtractor_1_out), .b(32'h1), .out(SBC), .bin(s1), .bout(C7));
  assign TST = A & B;  // AND_Gate and_1, 32 bits wide
  Subtractor #(.width(32)) subtractor_3 (.a({32{1'b0}}), .b(A), .out(RSB), .bout(C10));  // open: bin
  Subtractor #(.width(32)) subtractor_4 (.a(A), .b(B), .out(CMP), .bout(C11));  // open: bin
  Adder #(.width(32)) adder_2 (.a(A), .b(B), .out(CMN), .cout(C12));  // open: cin
  assign ORR = A | B;  // OR_Gate or_1, 32 bits wide
  assign BIC = A & not_2_out;  // AND_Gate and_2, 32 bits wide
  assign not_2_out = ~B;  // NOT_Gate not_2, 32 bits wide
  assign MVN = ~B;  // NOT_Gate not_3, 32 bits wide
  Negator #(.width(5)) negator_1 (.in(Shift), .out(negator_1_out));
  BitSelector #(.width(32)) bitselector_1 (.in(B), .out(C3), .sel(negator_1_out));
  Subtractor #(.width(5)) subtractor_5 (.a(Shift), .b(5'b00001), .out(subtractor_5_out));  // open: bin, bout
  BitSelector #(.width(32)) bitselector_2 (.in(B), .out(C45), .sel(subtractor_5_out));
  Multi32 multi32_1 (.in_1(A), .in_2(B), .out_3(MUL));
  BitSelector #(.width(32)) bitselector_3 (.in(S_t), .out(C8), .sel({5{1'b1}}));
  BitSelector #(.width(32)) bitselector_4 (.in(A), .out(bitselector_4_out), .sel({5{1'b1}}));
  BitSelector #(.width(32)) bitselector_5 (.in(B), .out(bitselector_5_out), .sel({5{1'b1}}));
  BitSelector #(.width(32)) bitselector_6 (.in(S), .out(bitselector_6_out), .sel({5{1'b1}}));
  Comparator #(.width(32)) comparator_1 (.a(S), .b({32{1'b0}}), .eq(Flags[1]), .lt(Flags[0]));  // open: gt
  xnor xnor_1 (xnor_1_out, bitselector_4_out, bitselector_5_out);
  xor xor_1 (xor_1_out, bitselector_5_out, bitselector_6_out);
  Multiplexer #(.select(4), .width(32), .enable("false")) multiplexer_1 (
    .in0(AAND), .in1(EOR), .in2(LSL), .in3(LSR), .in4(ASR), .in5(ADC), .in6(SBC), .in7(RROR), .in8(TST),
    .in9(RSB), .in10(CMP), .in11(CMN), .in12(ORR), .in13(MUL), .in14(BIC), .in15(MVN), .out(S), .sel(Codop));
  Multiplexer #(.select(4), .enable("false")) multiplexer_2 (
    .in0(1'b0), .in1(1'b0), .in2(C3), .in3(C45), .in4(C45), .in5(C6), .in6(C7), .in7(C8), .in8(1'b0),
    .in9(C10), .in10(C11), .in11(C12), .in12(1'b0), .in13(1'b0), .in14(1'b0), .in15(1'b0), .out(Flags[2]),
    .sel(Codop));
  and and_3 (Flags[3], xnor_1_out, xor_1_out);

  // Other names for the same wires on the sheet: N = Flags[0]; Z = Flags[1]; C = Flags[2]; V = Flags[3];
  //   Ouutput[31:0] = S
endmodule

module Multi32 (
  input  [31:0] in_1,
  input  [31:0] in_2,
  output [31:0] out_3
);

  wire [15:0] adder_1_out, bitselector_1_out, bitselector_2_out, bitselector_3_out, bitselector_4_out,
       multiplier_1_cout, multiplier_1_out, multiplier_2_out, multiplier_3_out;
  wire [31:0] bit_extender_1_out, bit_extender_2_out, shifter_1_out;

  BitSelector #(.width(32), .group(16)) bitselector_1 (.in(in_1), .out(bitselector_1_out), .sel(1'b0));
  BitSelector #(.width(32), .group(16)) bitselector_2 (.in(in_1), .out(bitselector_2_out), .sel(1'b1));
  BitSelector #(.width(32), .group(16)) bitselector_3 (.in(in_2), .out(bitselector_3_out), .sel(1'b0));
  BitSelector #(.width(32), .group(16)) bitselector_4 (.in(in_2), .out(bitselector_4_out), .sel(1'b1));
  Multiplier #(.width(16)) multiplier_1 (
    .a(bitselector_1_out), .b(bitselector_3_out), .out(multiplier_1_out), .cout(multiplier_1_cout));  // open: cin
  Multiplier #(.width(16)) multiplier_2 (
    .a(bitselector_1_out), .b(bitselector_4_out), .out(multiplier_2_out), .cin(multiplier_1_cout));  // open: cout
  Multiplier #(.width(16)) multiplier_3 (
    .a(bitselector_2_out), .b(bitselector_3_out), .out(multiplier_3_out));  // open: cin, cout
  assign bit_extender_1_out = {{16{multiplier_1_out[15]}}, multiplier_1_out};  // Bit_Extender bit_extender_1
  assign bit_extender_2_out = {{16{adder_1_out[15]}}, adder_1_out};  // Bit_Extender bit_extender_2
  Adder #(.width(16)) adder_1 (.a(multiplier_2_out), .b(multiplier_3_out), .out(adder_1_out));  // open: cin, cout
  Shifter #(.width(32)) shifter_1 (.in(bit_extender_2_out), .\dist (5'b10110), .out(shifter_1_out));
  assign out_3 = bit_extender_1_out | shifter_1_out;  // OR_Gate or_1, 32 bits wide
endmodule
