// Logisim project BancDeRegistre.circ as structural Verilog: 1 circuit, main circuit main
module main (
  input  [31:0] Aout,
  input  [31:0] DataIn,
  input  [2:0] RegA,
  input  [31:0] Bout,
  input  [2:0] RegB,
  input  in_6,
  input  [2:0] RegDest
);

  wire clock_1_out, demultiplexer_1_out0, demultiplexer_1_out1, demultiplexer_1_out2, demultiplexer_1_out3,
       demultiplexer_1_out4, demultiplexer_1_out5, demultiplexer_1_out6, demultiplexer_1_out7;
  wire [31:0] R0_q, R1_q, R2_q, R3_q, R4_q, R5_q, R6_q, R7_q;

  Clock clock_1 (.out(clock_1_out));
  Demultiplexer #(.select(3)) demultiplexer_1 (
    .out0(demultiplexer_1_out0), .out1(demultiplexer_1_out1), .out2(demultiplexer_1_out2),
    .out3(demultiplexer_1_out3), .out4(demultiplexer_1_out4), .out5(demultiplexer_1_out5),
    .out6(demultiplexer_1_out6), .out7(demultiplexer_1_out7), .in(clock_1_out), .sel(RegDest));  // open: en
  Register #(.width(32)) R0 (.D(DataIn), .Q(R0_q), .clk(demultiplexer_1_out0), .clr(in_6));  // open: en
  Register #(.width(32)) R1 (.D(DataIn), .Q(R1_q), .clk(demultiplexer_1_out1), .clr(in_6));  // open: en
  Register #(.width(32)) R2 (.D(DataIn), .Q(R2_q), .clk(demultiplexer_1_out2), .clr(in_6));  // open: en
  Register #(.width(32)) R3 (.D(DataIn), .Q(R3_q), .clk(demultiplexer_1_out3), .clr(in_6));  // open: en
  Register #(.width(32)) R4 (.D(DataIn), .Q(R4_q), .clk(demultiplexer_1_out4), .clr(in_6));  // open: en
  Register #(.width(32)) R5 (.D(DataIn), .Q(R5_q), .clk(demultiplexer_1_out5), .clr(in_6));  // open: en
  Register #(.width(32)) R6 (.D(DataIn), .Q(R6_q), .clk(demultiplexer_1_out6), .clr(in_6));  // open: en
  Register #(.width(32)) R7 (.D(DataIn), .Q(R7_q), .clk(demultiplexer_1_out7), .clr(in_6));  // open: en
  Multiplexer #(.select(3), .width(32)) multiplexer_1 (
    .in0(R0_q), .in1(R1_q), .in2(R2_q), .in3(R3_q), .in4(R4_q), .in5(R5_q), .in6(R6_q), .in7(R7_q),
    .out(Aout), .sel(RegA));  // open: en
  Multiplexer #(.select(3), .width(32)) multiplexer_2 (
    .in0(R0_q), .in1(R1_q), .in2(R2_q), .in3(R3_q), .in4(R4_q), .in5(R5_q), .in6(R6_q), .in7(R7_q),
    .out(Bout), .sel(RegB));  // open: en
endmodule
