// Logisim project Controller.circ as structural Verilog: 13 circuits, main circuit Controller
module Controller (
  input  [15:0] Inst,
  input  [3:0] Flags,
  input  Clk,
  input  Reset,
  output Carry,
  output DP_Shift,
  output Imm32_Enable,
  output [4:0] Imm5,
  output [31:0] Imm32,
  output [3:0] ALU_Opcode,
  output [2:0] Rm,
  output [2:0] Rn,
  output [2:0] Rd,
  output [31:0] RAM_Addr,
  output Load,
  output Store,
  output [7:0] PC
);

  wire Conditional_1_verified, Load_Store_1_pc_hold, not_1_out, Opcode_Decoder_1_conditional,
       Opcode_Decoder_1_data_processing, Opcode_Decoder_1_load_store, Opcode_Decoder_1_shift,
       Opcode_Decoder_1_sp_address, Shift_Add_Sub_Mov_1_p3, SP_Address_1_write_enable;
  wire [2:0] Data_Processing_1_rd, Data_Processing_1_rm, Data_Processing_1_rn, Load_Store_1_rd,
       Load_Store_1_rm, Shift_Add_Sub_Mov_1_p8, Shift_Add_Sub_Mov_1_p9, Shift_Add_Sub_Mov_1_p10;
  wire [3:0] Data_Processing_1_alu_opcode, Data_Processing_1_flags_update_mask, flags_apsr_1_flags_out,
       or_1_out, Shift_Add_Sub_Mov_1_p7, Shift_Add_Sub_Mov_1_p11;
  wire [7:0] adder_1_out, adder_2_out, Conditional_1_offset;
  wire [31:0] SP_Address_1_new_stack_pointer, Stack_Pointer_q;

  Register #(.width(32)) Stack_Pointer (
    .D(SP_Address_1_new_stack_pointer), .en(SP_Address_1_write_enable), .clk(Clk), .Q(Stack_Pointer_q),
    .clr(Reset));
  Opcode_Decoder Opcode_Decoder_1 (
    .Opcode(Inst[15:10]), .Data_Processing(Opcode_Decoder_1_data_processing),
    .SP_Address(Opcode_Decoder_1_sp_address), .Load_Store(Opcode_Decoder_1_load_store),
    .Conditional(Opcode_Decoder_1_conditional), .Shift(Opcode_Decoder_1_shift));
  assign or_1_out = Data_Processing_1_flags_update_mask | Shift_Add_Sub_Mov_1_p11;  // OR_Gate or_1, 4 bits wide
  // Shift_Add_Sub_Mov Shift_Add_Sub_Mov_1: pin names not known; wires that end beside it: Inst, Opcode_Decoder_1_data_processing, Shift_Add_Sub_Mov_1_p3, Imm32_Enable, Imm5, Imm32, Shift_Add_Sub_Mov_1_p7, Shift_Add_Sub_Mov_1_p8, Shift_Add_Sub_Mov_1_p9, Shift_Add_Sub_Mov_1_p10, Shift_Add_Sub_Mov_1_p11
  Data_Processing Data_Processing_1 (
    .ALU_Opcode(Data_Processing_1_alu_opcode), .Instruction(Inst), .Enable(Opcode_Decoder_1_sp_address),
    .Rm(Data_Processing_1_rm), .Rn(Data_Processing_1_rn), .Rd(Data_Processing_1_rd),
    .Flags_Update_Mask(Data_Processing_1_flags_update_mask));
  Flags_APSR flags_apsr_1 (
    .Flags_In(or_1_out), .Update_Mask(Flags), .Clk(Clk), .Rst(Reset), .Flags_Out(flags_apsr_1_flags_out));
  Load_Store Load_Store_1 (
    .Load(Load), .Store(Store), .Enable(Opcode_Decoder_1_load_store), .Rm(Load_Store_1_rm),
    .Rd(Load_Store_1_rd), .Stack_Pointer(Stack_Pointer_q), .RAM_Addr(RAM_Addr), .Instruction(Inst),
    .Clk(Clk), .Reset(Reset), .PC_Hold(Load_Store_1_pc_hold));
  Conditional Conditional_1 (
    .Instruction(Inst), .Verified(Conditional_1_verified), .Enable(Opcode_Decoder_1_shift),
    .Offset(Conditional_1_offset), .Z(flags_apsr_1_flags_out[2]), .V(flags_apsr_1_flags_out[0]),
    .N(flags_apsr_1_flags_out[3]), .C(flags_apsr_1_flags_out[1]));
  SP_Address SP_Address_1 (
    .New_Stack_Pointer(SP_Address_1_new_stack_pointer), .Stack_Pointer(Stack_Pointer_q),
    .Enable(Opcode_Decoder_1_conditional), .Instruction(Inst), .Write_Enable(SP_Address_1_write_enable));
  Adder adder_1 (.a(8'h3), .b(Conditional_1_offset), .out(adder_1_out), .cin(1'b0));  // open: cout
  Adder adder_2 (.a(adder_1_out), .b(PC), .out(adder_2_out), .cin(1'b0));  // open: cout
  and and_1 (DP_Shift, Opcode_Decoder_1_data_processing, ~Opcode_Decoder_1_sp_address);  // AND_Gate
  not not_1 (not_1_out, Load_Store_1_pc_hold);
  Counter counter_1 (
    .clr(Reset), .load(Conditional_1_verified), .up(1'b1), .count(not_1_out), .clk(Clk), .D(adder_2_out),
    .Q(PC));  // open: carry
  Multiplexer #(.enable("false")) multiplexer_1 (
    .in0(flags_apsr_1_flags_out[1]), .in1(Shift_Add_Sub_Mov_1_p3), .out(Carry), .sel(DP_Shift));
  assign ALU_Opcode = Shift_Add_Sub_Mov_1_p7 | Data_Processing_1_alu_opcode;  // OR_Gate or_2, 4 bits wide
  assign Rm = Shift_Add_Sub_Mov_1_p8 | Data_Processing_1_rm | Load_Store_1_rm;  // OR_Gate or_3, 3 bits wide
  assign Rn = Shift_Add_Sub_Mov_1_p9 | Data_Processing_1_rn;  // OR_Gate or_4, 3 bits wide
  assign Rd = Shift_Add_Sub_Mov_1_p10 | Data_Processing_1_rd | Load_Store_1_rd;  // OR_Gate or_5, 3 bits wide

  // Notes on the sheet:
  //   Extract carry
  //   Extract Opcode
  //   IF Reg_Imm=1 THEN use shift value from register ELSE use shift value from Imm5
  //   Buffer flags for next instruction
  //   Add 3 to offset because ARM pre-increments PC
  //   and does an additionnal prefect operation
endmodule

module Conditional (
  input  [15:0] Instruction,
  input  Enable,
  input  N,
  input  Z,
  input  C,
  input  V,
  output [7:0] Offset,
  output Verified
);

  wire [15:8] pull_resistor_1_node;

  Pull_Resistor pull_resistor_1 (.node({pull_resistor_1_node, Offset}));
  assign {pull_resistor_1_node, Offset} = Enable ? Instruction : 16'bz;  // Controlled_Buffer controlled_buffer_1
  Conditional_Check conditional_check_1 (
    .op0(pull_resistor_1_node[11]), .op1(pull_resistor_1_node[10]), .op2(pull_resistor_1_node[9]),
    .op3(pull_resistor_1_node[8]), .N(N), .Z(Z), .C(C), .V(V), .Enable(Verified));
endmodule

module Opcode_Decoder (
  input  [5:0] Opcode,
  output Data_Processing,
  output SP_Address,
  output Load_Store,
  output Conditional,
  output Shift
);

  wire not_1_out, not_2_out, not_3_out, not_4_out, not_5_out, not_6_out, not_7_out, not_8_out, not_9_out,
       not_10_out, not_11_out;

  not not_1 (not_1_out, Opcode[5]);
  not not_2 (not_2_out, Opcode[3]);
  not not_3 (not_3_out, Opcode[2]);
  not not_4 (not_4_out, Opcode[1]);
  not not_5 (not_5_out, Opcode[0]);
  not not_6 (not_6_out, Opcode[4]);
  not not_7 (not_7_out, Opcode[5]);
  not not_8 (not_8_out, Opcode[2]);
  not not_9 (not_9_out, Opcode[3]);
  not not_10 (not_10_out, Opcode[5]);
  not not_11 (not_11_out, Opcode[4]);
  and and_1 (Data_Processing, not_1_out, Opcode[4], not_2_out, not_3_out, not_4_out, not_5_out);
  and and_2 (SP_Address, Opcode[5], not_6_out, Opcode[3], Opcode[2]);
  and and_3 (Load_Store, not_7_out, Opcode[4], Opcode[3], not_8_out);
  and and_4 (Conditional, Opcode[5], Opcode[4], not_9_out, Opcode[2]);
  and and_5 (Shift, not_10_out, not_11_out);

  // Notes on the sheet:
  //   SP Address
  //   Load/Store
  //   Conditional branch
  //   Shift, add, sub, mov
  //   Data Processing
endmodule

module Data_Processing (
  input  [15:0] Instruction,
  input  Enable,
  output [2:0] Rn,
  output [2:0] Rm,
  output [2:0] Rd,
  output [3:0] Flags_Update_Mask,
  output [3:0] ALU_Opcode
);

  wire and_1_out, not_1_out, not_2_out;
  wire [15:10] Inst;

  assign {Inst, ALU_Opcode, Rm, Rd} = Enable ? Instruction : 16'bz;  // Controlled_Buffer controlled_buffer_1
  Pull_Resistor pull_resistor_1 (.node({Inst, ALU_Opcode, Rm, Rd}));
  not not_1 (not_1_out, ALU_Opcode[1]);
  and and_1 (and_1_out, ALU_Opcode[0], not_1_out, ALU_Opcode[3]);
  not not_2 (not_2_out, and_1_out);
  Pull_Resistor pull_resistor_2 (.node(Rn));
  assign Rn = not_2_out ? Rd : 3'bz;  // Controlled_Buffer controlled_buffer_2
  Flags_Data_Proc flags_data_proc_1 (
    .C(Flags_Update_Mask[1]), .Z(Flags_Update_Mask[2]), .N(Flags_Update_Mask[3]), .op0(ALU_Opcode[0]),
    .op1(ALU_Opcode[1]), .op2(ALU_Opcode[2]), .op3(ALU_Opcode[3]), .V(Flags_Update_Mask[0]));

  // Other names for the same wires on the sheet: Inst[9:0] = {ALU_Opcode, Rm, Rd}; Rn_t[2:0] = Rd;
  //   Op[3:0] = ALU_Opcode

  // Notes on the sheet:
  //   Pull output low on Enable = 0
  //   Note 2: RSB instruction has Rn as 1st operand.
  //   MUL instruction has Rn as 1st operand and Rdm as 2nd operand
  //   For simplification purposes, Rm is used for 1st operand both here and in the ALU.
  //   Note: instructions that does not save the result will still have the second operand as the destination register, the ALU will copy the second register to the destination register
endmodule

module Shift_Add_Sub_Mov (
  input  [15:0] Instruction,
  input  Enable,
  output [2:0] Rn,
  output [4:0] Imm5,
  output [2:0] Rm,
  output [2:0] Rd,
  output Imm32_Enable,
  output [31:0] Imm32,
  output [3:0] ALU_Opcode,
  output Carry,
  output [3:0] Flags_Update_Mask
);

  wire ADD, ADD_IMM, ADD_SUB, ADD_SUB_IMM, decode_operand_1_asr, decode_operand_1_lsl, decode_operand_1_lsr,
       i0, i1, i2, i3, i4, i5, i6, i7, i8, i9, i10, MOV, or_4_out, SHIFT, SUB, SUB_IMM;
  wire [1:0] or_5_out;
  wire [2:0] controlled_buffer_5_out;
  wire [3:0] flags_mask_shsm_1_v;
  wire [7:0] controlled_buffer_6_out;
  wire [15:11] Inst;
  wire [31:0] bit_extender_1_out, bit_extender_2_out;

  assign {Inst, i10, i9, i8, i7, i6, i5, i4, i3, i2, i1, i0} = Enable ? Instruction : 16'bz;  // Controlled_Buffer controlled_buffer_1
  Pull_Resistor pull_resistor_1 (.node({Inst, i10, i9, i8, i7, i6, i5, i4, i3, i2, i1, i0}));
  Opcode_Instruction opcode_instruction_1 (
    .op0(i9), .b0(ALU_Opcode[0]), .op1(i10), .b1(ALU_Opcode[1]), .op2(Inst[11]), .b2(ALU_Opcode[2]),
    .op3(Inst[12]), .b3(ALU_Opcode[3]));
  Decode_Operand decode_operand_1 (
    .ADD(ADD), .LSR(decode_operand_1_lsr), .op4(Inst[13]), .op2(Inst[11]), .op0(i9), .op1(i10),
    .op3(Inst[12]), .LSL(decode_operand_1_lsl), .ASR(decode_operand_1_asr), .SUB(SUB), .ADD_IMM(ADD_IMM),
    .SUB_IMM(SUB_IMM), .MOV(MOV));
  or or_1 (SHIFT, decode_operand_1_lsl, decode_operand_1_lsr, decode_operand_1_asr);
  or or_2 (ADD_SUB, ADD, SUB);
  or or_3 (ADD_SUB_IMM, ADD_IMM, SUB_IMM);
  // Probe on {i0, i1, i2, i3, i4, i5, i6, i7}
  or or_4 (or_4_out, SHIFT, ADD_SUB);
  or or_5 (or_5_out[0], ADD, ADD_IMM);
  or or_6 (or_5_out[1], SUB, SUB_IMM);
  Pull_Resistor pull_resistor_2 (.node(Rn));
  assign Rn = or_4_out ? {i5, i4, i3} : 3'bz;  // Controlled_Buffer controlled_buffer_2
  assign Imm5 = SHIFT ? {i10, i9, i8, i7, i6} : 5'bz;  // Controlled_Buffer controlled_buffer_3
  Pull_Resistor pull_resistor_3 (.node(Imm5));
  Pull_Resistor pull_resistor_4 (.node(Rm));
  assign Rm = ADD_SUB ? {i8, i7, i6} : 3'bz;  // Controlled_Buffer controlled_buffer_4
  Multiplexer #(.width(3), .enable("false")) multiplexer_1 (
    .in0({i2, i1, i0}), .in1({i10, i9, i8}), .out(Rd), .sel(MOV));
  assign controlled_buffer_5_out = ADD_SUB_IMM ? {i8, i7, i6} : 3'bz;  // Controlled_Buffer controlled_buffer_5
  or or_7 (Imm32_Enable, ADD_SUB_IMM, MOV);
  assign controlled_buffer_6_out = MOV ? {i0, i1, i2, i3, i4, i5, i6, i7} : 8'bz;  // Controlled_Buffer controlled_buffer_6
  Multiplexer #(.select(2), .enable("false")) multiplexer_2 (
    .in0(1'b0), .in1(1'b0), .in2(1'b1), .in3(1'b0), .out(Carry), .sel(or_5_out));
  // Probe on or_5_out
  Flags_Mask_SHSM flags_mask_shsm_1 (
    .C(flags_mask_shsm_1_v[1]), .Z(flags_mask_shsm_1_v[2]), .N(flags_mask_shsm_1_v[3]), .Move(MOV),
    .Imm(ADD_SUB_IMM), .Add_Sub(ADD_SUB), .Shift(SHIFT), .V(flags_mask_shsm_1_v[0]));
  Pull_Resistor pull_resistor_5 (.node(controlled_buffer_5_out));
  Pull_Resistor pull_resistor_6 (.node(controlled_buffer_6_out));
  assign Flags_Update_Mask = Enable ? flags_mask_shsm_1_v : 4'bz;  // Controlled_Buffer controlled_buffer_7
  assign bit_extender_1_out = {{29{1'b0}}, controlled_buffer_5_out};  // Bit_Extender bit_extender_1
  assign bit_extender_2_out = {{24{1'b0}}, controlled_buffer_6_out};  // Bit_Extender bit_extender_2
  Pull_Resistor pull_resistor_7 (.node(Flags_Update_Mask));
  assign Imm32 = bit_extender_1_out | bit_extender_2_out;  // OR_Gate or_8, 32 bits wide

  // Other names for the same wires on the sheet: En = Enable; Imm3[2:0] = {i8, i7, i6};
  //   Imm5_t[4:0] = {i10, i9, i8, i7, i6}; Imm8[7:0] = {i0, i1, i2, i3, i4, i5, i6, i7};
  //   Inst[10:0] = {i10, i9, i8, i7, i6, i5, i4, i3, i2, i1, i0}; Rm_t[2:0] = {i8, i7, i6}; Rn_t[2:0] = {i5, i4, i3};
  //   Rd_t[2:0] = {i2, i1, i0}; Rdm[2:0] = {i10, i9, i8}

  // Notes on the sheet:
  //   Pull output low on Enable = 0
  //   Note 3: Imm32_Enable forces the use of the immediate for Rm register
  //   Note: ALU uses Rn register for shifts. Use Rn instead of Rm for shifts (immediate) here too
  //   Note 2: MOV uses RSB ALU opcode with Imm8 reversed so that it is copied to output register
  //   Enable carry for SUB since it is reversed in ALU
  //   ALU will use Imm32 instead of Rm
endmodule

module Load_Store (
  input  [15:0] Instruction,
  input  Enable,
  input  [31:0] Stack_Pointer,
  input  Clk,
  input  Reset,
  output Store,
  output Load,
  output PC_Hold,
  output [2:0] Rm,
  output [2:0] Rd,
  output [31:0] RAM_Addr
);


  // Notes on the sheet:
  //   Delay load and hold PC for 1 cycle for the RAM to send out requested data 
endmodule

module SP_Address (
  input  Enable,
  input  [15:0] Instruction,
  input  [31:0] Stack_Pointer,
  output Write_Enable,
  output [31:0] New_Stack_Pointer
);


  // Notes on the sheet:
  //   Pull output low on Enable = 0
endmodule

module Flags_APSR (
  input  [3:0] Flags_In,
  input  [3:0] Update_Mask,
  input  Clk,
  input  Rst,
  output [3:0] Flags_Out
);
endmodule

module Decode_Operand (
  input  op0,
  input  op1,
  input  op2,
  input  op3,
  input  op4,
  output LSL,
  output LSR,
  output ASR,
  output ADD,
  output SUB,
  output ADD_IMM,
  output SUB_IMM,
  output MOV
);

  wire not_1_out, not_2_out, not_3_out, not_4_out, not_5_out, not_6_out, not_7_out, not_8_out, not_9_out,
       not_10_out, not_11_out, not_12_out, not_13_out, not_14_out, not_15_out, not_16_out, not_17_out;

  not not_1 (not_1_out, op2);
  not not_2 (not_2_out, op3);
  not not_3 (not_3_out, op4);
  not not_4 (not_4_out, op3);
  not not_5 (not_5_out, op4);
  not not_6 (not_6_out, op2);
  not not_7 (not_7_out, op4);
  not not_8 (not_8_out, op0);
  not not_9 (not_9_out, op1);
  not not_10 (not_10_out, op4);
  not not_11 (not_11_out, op1);
  not not_12 (not_12_out, op4);
  not not_13 (not_13_out, op0);
  not not_14 (not_14_out, op4);
  not not_15 (not_15_out, op4);
  not not_16 (not_16_out, op2);
  not not_17 (not_17_out, op3);
  and and_1 (LSL, not_1_out, not_2_out, not_3_out);
  and and_2 (LSR, op2, not_4_out, not_5_out);
  and and_3 (ASR, not_6_out, op3, not_7_out);
  and and_4 (ADD, not_8_out, not_9_out, op2, op3, not_10_out);
  and and_5 (SUB, op0, not_11_out, op2, op3, not_12_out);
  and and_6 (ADD_IMM, not_13_out, op1, op2, op3, not_14_out);
  and and_7 (SUB_IMM, op0, op1, op2, op3, not_15_out);
  and and_8 (MOV, not_16_out, not_17_out, op4);
endmodule

module Opcode_Instruction (
  input  op0,
  input  op1,
  input  op2,
  input  op3,
  output b0,
  output b1,
  output b2,
  output b3
);

  wire and_1_out, and_2_out, and_3_out, not_1_out, not_2_out, not_3_out;

  not not_1 (not_1_out, op3);
  and and_1 (and_1_out, op0, op2);
  not not_2 (not_2_out, op0);
  and and_2 (and_2_out, not_2_out, op2);
  and and_3 (and_3_out, op2, not_3_out);
  not not_3 (not_3_out, op3);
  or or_1 (b2, not_1_out, and_1_out);
  or or_2 (b3, and_2_out, and_3_out);

  assign b0 = 1'b0;
  assign b1 = op3;
endmodule

module Flags_Mask_SHSM (
  input  Shift,
  input  Add_Sub,
  input  Imm,
  input  Move,
  output N,
  output Z,
  output C,
  output V
);

  wire and_1_out, and_2_out, and_3_out, and_4_out, and_5_out, and_6_out, and_7_out, and_8_out, and_9_out,
       and_10_out, and_11_out, and_12_out, and_13_out, not_1_out, not_2_out, not_3_out, not_4_out, not_5_out,
       not_6_out, not_7_out, not_8_out, not_9_out, not_10_out, not_11_out, not_12_out, not_13_out,
       not_14_out, not_15_out, not_16_out, not_17_out, not_18_out, not_19_out, not_20_out, not_21_out,
       not_22_out, not_23_out, not_24_out, not_25_out, not_26_out, not_27_out, not_28_out, not_29_out,
       not_30_out, not_31_out, not_32_out, not_33_out, not_34_out, not_35_out, not_36_out, not_37_out,
       not_38_out, not_39_out;

  not not_1 (not_1_out, Shift);
  not not_2 (not_2_out, Add_Sub);
  not not_3 (not_3_out, Imm);
  not not_4 (not_4_out, Shift);
  not not_5 (not_5_out, Add_Sub);
  not not_6 (not_6_out, Move);
  not not_7 (not_7_out, Shift);
  not not_8 (not_8_out, Imm);
  not not_9 (not_9_out, Move);
  not not_10 (not_10_out, Add_Sub);
  not not_11 (not_11_out, Imm);
  not not_12 (not_12_out, Move);
  not not_13 (not_13_out, Shift);
  not not_14 (not_14_out, Add_Sub);
  not not_15 (not_15_out, Imm);
  not not_16 (not_16_out, Shift);
  not not_17 (not_17_out, Add_Sub);
  not not_18 (not_18_out, Move);
  not not_19 (not_19_out, Shift);
  not not_20 (not_20_out, Imm);
  not not_21 (not_21_out, Move);
  not not_22 (not_22_out, Add_Sub);
  not not_23 (not_23_out, Imm);
  not not_24 (not_24_out, Move);
  not not_25 (not_25_out, Shift);
  not not_26 (not_26_out, Add_Sub);
  not not_27 (not_27_out, Move);
  not not_28 (not_28_out, Shift);
  not not_29 (not_29_out, Imm);
  not not_30 (not_30_out, Move);
  not not_31 (not_31_out, Add_Sub);
  not not_32 (not_32_out, Imm);
  not not_33 (not_33_out, Move);
  not not_34 (not_34_out, Shift);
  not not_35 (not_35_out, Add_Sub);
  not not_36 (not_36_out, Move);
  not not_37 (not_37_out, Shift);
  not not_38 (not_38_out, Imm);
  not not_39 (not_39_out, Move);
  and and_1 (and_1_out, not_1_out, not_2_out, not_3_out, Move);
  and and_2 (and_2_out, not_4_out, not_5_out, Imm, not_6_out);
  and and_3 (and_3_out, not_7_out, Add_Sub, not_8_out, not_9_out);
  and and_4 (and_4_out, Shift, not_10_out, not_11_out, not_12_out);
  and and_5 (and_5_out, not_13_out, not_14_out, not_15_out, Move);
  and and_6 (and_6_out, not_16_out, not_17_out, Imm, not_18_out);
  and and_7 (and_7_out, not_19_out, Add_Sub, not_20_out, not_21_out);
  and and_8 (and_8_out, Shift, not_22_out, not_23_out, not_24_out);
  and and_9 (and_9_out, not_25_out, not_26_out, Imm, not_27_out);
  or or_1 (C, and_9_out, and_10_out, and_11_out);
  and and_10 (and_10_out, not_28_out, Add_Sub, not_29_out, not_30_out);
  and and_11 (and_11_out, Shift, not_31_out, not_32_out, not_33_out);
  and and_12 (and_12_out, not_34_out, not_35_out, Imm, not_36_out);
  or or_2 (V, and_12_out, and_13_out);
  and and_13 (and_13_out, not_37_out, Add_Sub, not_38_out, not_39_out);
  or or_3 (N, and_1_out, and_2_out, and_3_out, and_4_out);
  or or_4 (Z, and_5_out, and_6_out, and_7_out, and_8_out);
endmodule

module Conditional_Check (
  input  op0,
  input  op1,
  input  op2,
  input  op3,
  input  N,
  input  Z,
  input  C,
  input  V,
  output Enable
);

  wire and_1_out, and_2_out, and_3_out, and_4_out, and_5_out, and_6_out, and_7_out, and_8_out, and_9_out,
       and_10_out, and_11_out, and_12_out, and_13_out, and_14_out, and_15_out, and_16_out, and_17_out,
       and_18_out, and_19_out, and_20_out, and_21_out, and_22_out, and_23_out, not_1_out, not_2_out,
       not_3_out, not_4_out, not_5_out, not_6_out, not_7_out, not_8_out, not_9_out, not_10_out, not_11_out,
       not_12_out, not_13_out, not_14_out, not_15_out, not_16_out, not_17_out, not_18_out, not_19_out,
       not_20_out, not_21_out, not_22_out, not_23_out, not_24_out, not_25_out, not_26_out, not_27_out,
       not_28_out, not_29_out, not_30_out, not_31_out, not_32_out, not_33_out, not_34_out, not_35_out,
       not_36_out, not_37_out, not_38_out, not_39_out, not_40_out, not_41_out, not_42_out, not_43_out,
       not_44_out, not_45_out, not_46_out, not_47_out, or_1_out, or_2_out, or_3_out, or_4_out;

  not not_1 (not_1_out, N);
  not not_2 (not_2_out, V);
  not not_3 (not_3_out, V);
  not not_4 (not_4_out, N);
  and and_1 (and_1_out, N, V);
  not not_5 (not_5_out, N);
  and and_2 (and_2_out, not_5_out, not_6_out);
  not not_6 (not_6_out, V);
  and and_3 (and_3_out, N, not_7_out);
  not not_7 (not_7_out, V);
  not not_8 (not_8_out, N);
  and and_4 (and_4_out, not_8_out, V);
  not not_9 (not_9_out, op0);
  not not_10 (not_10_out, op1);
  not not_11 (not_11_out, op2);
  not not_12 (not_12_out, op3);
  not not_13 (not_13_out, op0);
  not not_14 (not_14_out, op1);
  not not_15 (not_15_out, op2);
  not not_16 (not_16_out, Z);
  not not_17 (not_17_out, op0);
  not not_18 (not_18_out, op1);
  not not_19 (not_19_out, op3);
  not not_20 (not_20_out, op0);
  not not_21 (not_21_out, op1);
  not not_22 (not_22_out, C);
  not not_23 (not_23_out, op0);
  not not_24 (not_24_out, op2);
  not not_25 (not_25_out, op3);
  not not_26 (not_26_out, op0);
  not not_27 (not_27_out, op2);
  not not_28 (not_28_out, N);
  not not_29 (not_29_out, op0);
  not not_30 (not_30_out, op3);
  not not_31 (not_31_out, op0);
  not not_32 (not_32_out, V);
  not not_33 (not_33_out, op1);
  not not_34 (not_34_out, op2);
  not not_35 (not_35_out, op3);
  not not_36 (not_36_out, V);
  not not_37 (not_37_out, op1);
  not not_38 (not_38_out, op2);
  not not_39 (not_39_out, C);
  not not_40 (not_40_out, op1);
  not not_41 (not_41_out, op3);
  and and_5 (and_5_out, N, V);
  or or_1 (or_1_out, and_5_out, and_6_out);
  and and_6 (and_6_out, not_1_out, not_2_out);
  not not_42 (not_42_out, op1);
  and and_7 (and_7_out, N, not_3_out);
  or or_2 (or_2_out, and_7_out, and_8_out);
  and and_8 (and_8_out, not_4_out, V);
  not not_43 (not_43_out, op2);
  not not_44 (not_44_out, op3);
  not not_45 (not_45_out, Z);
  or or_3 (or_3_out, and_1_out, and_2_out);
  not not_46 (not_46_out, op2);
  or or_4 (or_4_out, and_3_out, and_4_out);
  not not_47 (not_47_out, op3);
  and and_9 (and_9_out, not_9_out, not_10_out, not_11_out, not_12_out, Z);
  and and_10 (and_10_out, not_13_out, not_14_out, not_15_out, op3, not_16_out);
  and and_11 (and_11_out, not_17_out, not_18_out, op2, not_19_out, C);
  and and_12 (and_12_out, not_20_out, not_21_out, op2, op3, not_22_out);
  and and_13 (and_13_out, not_23_out, op1, not_24_out, not_25_out, N);
  and and_14 (and_14_out, not_26_out, op1, not_27_out, op3, not_28_out);
  and and_15 (and_15_out, not_29_out, op1, op2, not_30_out, V);
  and and_16 (and_16_out, not_31_out, op1, op2, op3, not_32_out);
  and and_17 (and_17_out, op0, not_33_out, not_34_out, not_35_out, C, not_36_out);
  and and_18 (and_18_out, op0, not_37_out, not_38_out, op3, not_39_out, Z);
  and and_19 (and_19_out, op0, not_40_out, op2, not_41_out, or_1_out);
  and and_20 (and_20_out, op0, not_42_out, op2, op3, or_2_out);
  and and_21 (and_21_out, op0, op1, not_43_out, not_44_out, not_45_out, or_3_out);
  and and_22 (and_22_out, op0, op1, not_46_out, op3, Z, or_4_out);
  and and_23 (and_23_out, op0, op1, op2, not_47_out);
  or or_5 (Enable, and_9_out, and_10_out, and_11_out, and_12_out, and_13_out, and_14_out, and_15_out, and_16_out, and_17_out, and_18_out, and_19_out, and_20_out, and_21_out, and_22_out, and_23_out);
endmodule

module Flags_Data_Proc (
  input  op3,
  input  op2,
  input  op1,
  input  op0,
  output N,
  output Z,
  output C,
  output V
);

  wire and_1_out, and_2_out, and_3_out, and_4_out, nand_1_out, nand_2_out, nand_3_out, not_1_out, not_2_out,
       not_3_out, not_4_out, not_5_out, not_6_out, not_7_out, not_8_out, not_9_out, not_10_out, not_11_out;

  not not_1 (not_1_out, op3);
  not not_2 (not_2_out, op2);
  not not_3 (not_3_out, op0);
  not not_4 (not_4_out, op1);
  not not_5 (not_5_out, op3);
  not not_6 (not_6_out, op1);
  not not_7 (not_7_out, op3);
  not not_8 (not_8_out, op0);
  not not_9 (not_9_out, op2);
  not not_10 (not_10_out, op1);
  not not_11 (not_11_out, op2);
  nand nand_1 (nand_1_out, not_1_out, op2, op1, op0);
  nand nand_2 (nand_2_out, op3, not_2_out, op1, not_3_out);
  nand nand_3 (nand_3_out, op3, op2, not_4_out, op0);
  and and_1 (and_1_out, not_5_out, op2, not_6_out, op0);
  and and_2 (and_2_out, not_7_out, op2, op1, not_8_out);
  and and_3 (and_3_out, op3, not_9_out, not_10_out, op0);
  and and_4 (and_4_out, op3, not_11_out, op1, op0);
  and and_5 (C, nand_1_out, nand_2_out, nand_3_out);
  or or_1 (V, and_1_out, and_2_out, and_3_out, and_4_out);

  assign N = 1'b1;
  assign Z = 1'b1;
endmodule
